# Fritzing sketch design_master (saved by Fritzing 0.9.3b)
breadboards: 1

parts:
  Composant1 = Arduino Pro Mini v13  # not connected
  S1 = Pushbutton [package="[THT]"]

nets:
  N1: S1.Pin_1, S1.Pin_2
  N2: S1.Pin_3, S1.Pin_4
